// Logisim project Processor.circ as structural Verilog
module Register_File (
  input  [15:0] Write_Data,
  input  [1:0] Read_Register_1,
  input  [1:0] Write_on_Registor,
  input  [1:0] Read_Register_2,
  input  Write,
  input  Clock_Pulse,
  output [15:0] Read_Data1,
  output [15:0] Read_Data_2
);

  wire and_1_out, and_2_out, and_3_out, and_4_out, decoder_1_out0, decoder_1_out1, decoder_1_out2;
  wire [15:0] register_1_q, register_2_q, register_3_q, register_4_q;

  Decoder #(.select(2)) decoder_1 (
    .out0(decoder_1_out0), .out1(decoder_1_out1), .out2(decoder_1_out2), .sel(Write_on_Registor));  // open: out3, en
  and and_1 (and_1_out, decoder_1_out0, Write);
  and and_2 (and_2_out, decoder_1_out1, Write);
  and and_3 (and_3_out, decoder_1_out2, Write);
  and and_4 (and_4_out, decoder_1_out2, Write);
  Register #(.width(16)) register_1 (.D(Write_Data), .en(and_1_out), .Q(register_1_q), .clk(Clock_Pulse));  // open: clr
  Register #(.width(16)) register_2 (.D(Write_Data), .en(and_2_out), .Q(register_2_q), .clk(Clock_Pulse));  // open: clr
  Register #(.width(16)) register_3 (.D(Write_Data), .en(and_3_out), .Q(register_3_q), .clk(Clock_Pulse));  // open: clr
  Register #(.width(16)) register_4 (.D(Write_Data), .en(and_4_out), .Q(register_4_q), .clk(Clock_Pulse));  // open: clr
  Multiplexer #(.select(2), .width(16)) multiplexer_1 (
    .in0(register_1_q), .in1(register_2_q), .in2(register_3_q), .in3(register_4_q), .out(Read_Data1),
    .sel(Read_Register_1));  // open: en
  Multiplexer #(.select(2), .width(16)) multiplexer_2 (
    .in0(register_1_q), .in1(register_2_q), .in2(register_4_q), .in3(register_4_q), .out(Read_Data_2),
    .sel(Read_Register_2));  // open: en
endmodule
